# Fritzing sketch circuitry (saved by Fritzing 1.0.6)

parts:
  Part1 = Adafruit Metro ESP32-S3 [part_number="Adafruit #5500"]
  Part2 = Motor Driver 1A Dual TB6612FNG
  DC_Mot_Enc1 = DC Motor with two-phase hall-encoder [part_number=VT-E-G25A-06-177E]
  DC_Mot_Enc2 = DC Motor with two-phase hall-encoder [part_number=VT-E-G25A-06-177E]
  MPU-1 = Adafruit MPU6050
  U1 = LIPO-110mAh [package=lipo-110]  # not connected
  U2 = LIPO-2000mAh [package=lipo-2000]

nets:
  N1: Part1.SDA, MPU-1.SDA
  N2: Part1.SCL, MPU-1.SCL
  VCC: Part1.3.3V, Part2.VCC, MPU-1.VCC
  GND: Part1.GND, Part2.GND, MPU-1.GND, U2.-
  N3: Part1.D12, DC_Mot_Enc1.pin6
  N4: Part1.D11, DC_Mot_Enc1.pin4
  N5: Part1.D10, DC_Mot_Enc2.pin6
  N6: Part1.D9, DC_Mot_Enc2.pin4
  N7: Part1.D8, Part2.PWMB
  N8: Part1.D7, Part2.BIN2
  N9: Part1.D6, Part2.BIN1
  N10: Part1.D5, Part2.STBY
  N11: Part1.D4, Part2.AIN1
  N12: Part1.D3, Part2.AIN2
  N13: Part1.D2, Part2.PWMA
  N14: Part2.B01, DC_Mot_Enc1.pin2
  N15: Part2.B02, DC_Mot_Enc1.pin1
  N16: Part2.A01, DC_Mot_Enc2.pin1
  N17: Part2.VM, U2.+

custom parts:
  Adafruit Metro ESP32-S3: What's Metro-shaped and has an ESP32-S3 WiFi module? What has a STEMMA QT connector for I2C devices and a Lipoly charger circuit? What has your favorite Espressif WiFi microcontroller and lots of memory for your next IoT project? That's right - it's the new Adafruit Metro ESP32-S3! With native USB and a load of PSRAM, this board is perfect for use with CircuitPython or Arduino to add low-cost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
  Adafruit MPU6050: The MPU-6050 is a popular six axis accelerometer and gyroscope (gyro) that has all the info you need on how things are shakin' and spinnin' . With six axes of sensing and 16-bit measurements, you'll have everything you need to give your robot friend an inner ear. This combination of gyroscopes and accelerometers is commonly referred to as an Inertial Measurement Unit or IMU. Not so long ago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
